# Fritzing sketch audioguies (saved by Fritzing 0.9.10b)

parts:
  R1 = Resistor [tolerance=±5% resistance=100 package="1206 [SMD]"]
  LED1 = LED - 3mm [color="Green (560nm)" current=0A package="3 mm [THT]"]
  TRRS1 = Audio Jack (TRS) 3.5mm [package="4Ucon 08780 [THT]"]
  S3 = Toggle Switch [package=THT]
  Part1 = Arduino Nano (Rev3.0)
  A1 = DFPlayer Pro-a mini
  VCC1 = Battery block 9V
  VMA405 = RFID-RC522-v3
  S2 = Momentary Switch [package=ksa_sealed_tac_switch]

nets:
  N1: R1.Pin_0, LED1.anode
  N2: R1.Pin_1, Part1.A2
  N3: LED1.cathode, VCC1.-
  GND: TRRS1.Sleeve, Part1.GND, A1.Pin_2, VMA405.GND, S2.1
  N4: TRRS1.Tip, A1.Pin_5, A1.Pin_6
  N5: S3.L1, Part1.VIN
  N6: S3.COM, VCC1.+
  N7: Part1.D2, VMA405.IRQ
  N8: Part1.D6, A1.Pin_4
  N9: Part1.D7, A1.Pin_3
  N10: Part1.D9, VMA405.RST
  N11: Part1.D10, VMA405.SDA
  N12: Part1.D11/MOSI, VMA405.MOSI
  N13: Part1.D12/MISO, VMA405.MISO
  N14: Part1.A3, S2.3
  3V3: Part1.3V3, A1.Pin_1, VMA405.3.3V
  N15: Part1.D13/SCK, VMA405.SCK

custom parts:
  DFPlayer Pro-a mini: DFPlayer Pro-a mini simple but powerful MP3 Player.
  RFID-RC522-v3: A simple China made RFID-RC522 Reader (6x4 cm); do check the pin labels, as this is a MFRC522 based clone.
